// Digital circuit 16bitadder.dig as structural Verilog
module _16bitadder (
  input  [15:0] xin,
  input  zx,
  input  nx,
  input  ny,
  input  zy,
  input  [15:0] yin,
  output [15:0] x_plus_y
);

  wire _7483_1_pin14, _7483_2_pin14, _7483_3_pin14;
  wire [3:0] _7483_1_pin11, _7483_2_pin11, _7483_3_pin11, _7483_4_pin11;
  wire [15:0] xproc_1_xproc;

  xproc xproc_1 (.X(xin), .zx(zx), .nx(nx), .xproc(xproc_1_xproc));
  _7483 _7483_1 (
    .pin1(xproc_1_xproc[3]), .pin2(x_plus_y[2]), .pin3(xproc_1_xproc[2]), .pin4(_7483_1_pin11[2]),
    .pin5(1'b1), .pin6(x_plus_y[1]), .pin7(_7483_1_pin11[1]), .pin8(xproc_1_xproc[1]), .pin9(x_plus_y[0]),
    .pin10(xproc_1_xproc[0]), .pin11(_7483_1_pin11[0]), .pin12(1'b0), .pin13(1'b0), .pin14(_7483_1_pin14),
    .pin15(x_plus_y[3]), .pin16(_7483_1_pin11[3]));
  _7483 _7483_2 (
    .pin1(xproc_1_xproc[7]), .pin2(x_plus_y[6]), .pin3(xproc_1_xproc[6]), .pin4(_7483_2_pin11[2]),
    .pin5(1'b1), .pin6(x_plus_y[5]), .pin7(_7483_2_pin11[1]), .pin8(xproc_1_xproc[5]), .pin9(x_plus_y[4]),
    .pin10(xproc_1_xproc[4]), .pin11(_7483_2_pin11[0]), .pin12(1'b0), .pin13(_7483_1_pin14),
    .pin14(_7483_2_pin14), .pin15(x_plus_y[7]), .pin16(_7483_2_pin11[3]));
  _7483 _7483_3 (
    .pin1(xproc_1_xproc[11]), .pin2(x_plus_y[10]), .pin3(xproc_1_xproc[10]), .pin4(_7483_3_pin11[2]),
    .pin5(1'b1), .pin6(x_plus_y[9]), .pin7(_7483_3_pin11[1]), .pin8(xproc_1_xproc[9]), .pin9(x_plus_y[8]),
    .pin10(xproc_1_xproc[8]), .pin11(_7483_3_pin11[0]), .pin12(1'b0), .pin13(_7483_2_pin14),
    .pin14(_7483_3_pin14), .pin15(x_plus_y[11]), .pin16(_7483_3_pin11[3]));
  _7483 _7483_4 (
    .pin1(xproc_1_xproc[15]), .pin2(x_plus_y[14]), .pin3(xproc_1_xproc[14]), .pin4(_7483_4_pin11[2]),
    .pin5(1'b1), .pin6(x_plus_y[13]), .pin7(_7483_4_pin11[1]), .pin8(xproc_1_xproc[13]), .pin9(x_plus_y[12]),
    .pin10(xproc_1_xproc[12]), .pin11(_7483_4_pin11[0]), .pin12(1'b0), .pin13(_7483_3_pin14),
    .pin15(x_plus_y[15]), .pin16(_7483_4_pin11[3]));  // open: pin14
  xproc xproc_2 (.X(yin), .zx(zy), .nx(ny), .xproc({_7483_4_pin11, _7483_3_pin11, _7483_2_pin11, _7483_1_pin11}));
endmodule
