// Digital circuit 16bitand.dig as structural Verilog
module _16bitand (
  input  [15:0] x,
  input  ny,
  input  zy,
  input  [15:0] y,
  input  zx,
  input  nx,
  output [15:0] x_y
);

  wire [15:0] _7408_1_pin2, yproc_xproc;

  xproc yproc (.X(x), .zx(zx), .nx(nx), .xproc(yproc_xproc));
  _7408 _7408_1 (
    .pin1(yproc_xproc[0]), .pin2(_7408_1_pin2[0]), .pin3(x_y[0]), .pin4(yproc_xproc[1]),
    .pin5(_7408_1_pin2[1]), .pin6(x_y[1]), .pin7(1'b0), .pin8(x_y[2]), .pin9(yproc_xproc[2]),
    .pin10(_7408_1_pin2[2]), .pin11(x_y[3]), .pin12(yproc_xproc[3]), .pin13(_7408_1_pin2[3]), .pin14(1'b1));
  _7408 _7408_2 (
    .pin1(yproc_xproc[4]), .pin2(_7408_1_pin2[4]), .pin3(x_y[4]), .pin4(yproc_xproc[5]),
    .pin5(_7408_1_pin2[5]), .pin6(x_y[5]), .pin7(1'b0), .pin8(x_y[6]), .pin9(yproc_xproc[6]),
    .pin10(_7408_1_pin2[6]), .pin11(x_y[7]), .pin12(yproc_xproc[7]), .pin13(_7408_1_pin2[7]), .pin14(1'b1));
  _7408 _7408_3 (
    .pin1(yproc_xproc[8]), .pin2(_7408_1_pin2[8]), .pin3(x_y[8]), .pin4(yproc_xproc[9]),
    .pin5(_7408_1_pin2[9]), .pin6(x_y[9]), .pin7(1'b0), .pin8(x_y[10]), .pin9(yproc_xproc[10]),
    .pin10(_7408_1_pin2[10]), .pin11(x_y[11]), .pin12(yproc_xproc[11]), .pin13(_7408_1_pin2[11]), .pin14(1'b1));
  _7408 _7408_4 (
    .pin1(yproc_xproc[12]), .pin2(_7408_1_pin2[12]), .pin3(x_y[12]), .pin4(yproc_xproc[13]),
    .pin5(_7408_1_pin2[13]), .pin6(x_y[13]), .pin7(1'b0), .pin8(x_y[14]), .pin9(yproc_xproc[14]),
    .pin10(_7408_1_pin2[14]), .pin11(x_y[15]), .pin12(yproc_xproc[15]), .pin13(_7408_1_pin2[15]), .pin14(1'b1));
  xproc yproc_2 (.X(y), .zx(zy), .nx(ny), .xproc(_7408_1_pin2));
endmodule
