// Digital circuit ALU.dig as structural Verilog
module ALU (
  input  [15:0] x,
  input  [15:0] y,
  input  f,
  input  nx,
  input  ny,
  input  zx,
  input  zy,
  input  no,
  output [15:0] out,
  output ng,
  output zr
);

  wire _7432_1_pin3, _7432_1_pin6, _7432_1_pin8, _7432_1_pin11, _7432_2_pin3, _7432_2_pin6, _7432_2_pin8,
       _7432_2_pin11, _7432_3_pin3, _7432_3_pin6, _7432_3_pin8, _7432_3_pin11, _7432_4_pin3, _7432_4_pin6,
       _7432_4_pin8;
  wire [15:0] _16bitadder_1_x_plus_y, _16bitand_1_x_y, mux16_1_out, x_inv_1_x_out;

  _16bitand _16bitand_1 (.x(x), .ny(ny), .zy(zy), .y(y), .zx(zx), .nx(nx), .x_y(_16bitand_1_x_y));
  _16bitadder _16bitadder_1 (.xin(x), .zx(zx), .nx(nx), .ny(ny), .zy(zy), .yin(y), .x_plus_y(_16bitadder_1_x_plus_y));
  Mux16 mux16_1 (.sel(f), .in0(_16bitand_1_x_y), .in1(_16bitadder_1_x_plus_y), .out(mux16_1_out));
  x_inv x_inv_1 (.x_in(mux16_1_out), .x_out(x_inv_1_x_out));
  Mux16 mux16_2 (.sel(no), .in0(mux16_1_out), .in1(x_inv_1_x_out), .out({ng, out[14:0]}));
  _7432 _7432_1 (
    .pin1(out[0]), .pin2(out[1]), .pin3(_7432_1_pin3), .pin4(out[2]), .pin5(out[3]), .pin6(_7432_1_pin6),
    .pin7(1'b0), .pin8(_7432_1_pin8), .pin9(out[4]), .pin10(out[5]), .pin11(_7432_1_pin11), .pin12(out[6]),
    .pin13(out[7]), .pin14(1'b1));
  _7432 _7432_2 (
    .pin1(out[8]), .pin2(out[9]), .pin3(_7432_2_pin3), .pin4(out[10]), .pin5(out[11]), .pin6(_7432_2_pin6),
    .pin7(1'b0), .pin8(_7432_2_pin8), .pin9(out[12]), .pin10(out[13]), .pin11(_7432_2_pin11),
    .pin12(out[14]), .pin13(ng), .pin14(1'b1));
  _7432 _7432_3 (
    .pin1(_7432_1_pin3), .pin2(_7432_1_pin6), .pin3(_7432_3_pin3), .pin4(_7432_1_pin8), .pin5(_7432_1_pin11),
    .pin6(_7432_3_pin6), .pin7(1'b0), .pin8(_7432_3_pin8), .pin9(_7432_2_pin3), .pin10(_7432_2_pin6),
    .pin11(_7432_3_pin11), .pin12(_7432_2_pin8), .pin13(_7432_2_pin11), .pin14(1'b1));
  _7432 _7432_4 (
    .pin1(_7432_3_pin3), .pin2(_7432_3_pin6), .pin3(_7432_4_pin3), .pin4(_7432_4_pin3), .pin5(_7432_3_pin8),
    .pin6(_7432_4_pin6), .pin7(1'b0), .pin8(_7432_4_pin8), .pin9(_7432_4_pin6), .pin10(_7432_3_pin11),
    .pin12(1'b1), .pin13(1'b1), .pin14(1'b1));  // open: pin11
  _7404 _7404_1 (
    .pin1(_7432_4_pin8), .pin2(zr), .pin3(1'b0), .pin5(1'b0), .pin7(1'b0), .pin9(1'b1), .pin11(1'b1),
    .pin13(1'b1), .pin14(1'b1));  // open: pin4, pin6, pin8, pin10, pin12

  assign out[15] = ng;
endmodule
