// Digital circuit Add1.dig as structural Verilog
module Add1 (
  input  [15:0] x,
  output [15:0] x_plus_1
);

  wire _7483_1_pin14, _7483_2_pin13, _7483_2_pin14;

  _7483 _7483_1 (
    .pin1(x[3]), .pin2(x_plus_1[2]), .pin3(x[2]), .pin4(1'b0), .pin5(1'b1), .pin6(x_plus_1[1]), .pin7(1'b0),
    .pin8(x[1]), .pin9(x_plus_1[0]), .pin10(x[0]), .pin11(1'b1), .pin12(1'b0), .pin13(1'b0),
    .pin14(_7483_1_pin14), .pin15(x_plus_1[3]), .pin16(1'b0));
  _7483 _7483_2 (
    .pin1(x[11]), .pin2(x_plus_1[10]), .pin3(x[10]), .pin4(1'b0), .pin5(1'b1), .pin6(x_plus_1[9]),
    .pin7(1'b0), .pin8(x[9]), .pin9(x_plus_1[8]), .pin10(x[8]), .pin11(1'b0), .pin12(1'b0),
    .pin13(_7483_2_pin13), .pin14(_7483_2_pin14), .pin15(x_plus_1[11]), .pin16(1'b0));
  _7483 _7483_3 (
    .pin1(x[7]), .pin2(x_plus_1[6]), .pin3(x[6]), .pin4(1'b0), .pin5(1'b1), .pin6(x_plus_1[5]), .pin7(1'b0),
    .pin8(x[5]), .pin9(x_plus_1[4]), .pin10(x[4]), .pin11(1'b0), .pin12(1'b0), .pin13(_7483_1_pin14),
    .pin14(_7483_2_pin13), .pin15(x_plus_1[7]), .pin16(1'b0));
  _7483 _7483_4 (
    .pin1(x[15]), .pin2(x_plus_1[14]), .pin3(x[14]), .pin4(1'b0), .pin5(1'b1), .pin6(x_plus_1[13]),
    .pin7(1'b0), .pin8(x[13]), .pin9(x_plus_1[12]), .pin10(x[12]), .pin11(1'b0), .pin12(1'b0),
    .pin13(_7483_2_pin14), .pin15(x_plus_1[15]), .pin16(1'b0));  // open: pin14
endmodule
