// Digital circuit CPU.dig as structural Verilog
module CPU (
  input  [15:0] instruction,
  input  [15:0] in_m,
  input  clk,
  input  reset,
  output [15:0] outM,
  output writeM,
  output [14:0] AddressM,
  output [14:0] pc,
  output [15:0] regAvalue,
  output [15:0] regDvalue
);

  wire _7408_1_pin3, _7408_2_pin3, _7408_2_pin6, _7408_2_pin8, _7408_3_pin3, _7408_3_pin6, _7408_3_pin8,
       _7408_3_pin9, _7432_1_pin3, _7432_1_pin6, _7432_1_pin8, _74157_1_pin4, alu_1_ng, alu_1_zr;
  wire [15:0] mux16_1_out, mux16_2_out;
  wire [15:15] pc_1_count_out;

  _74157 _74157_1 (
    .pin1(instruction[15]), .pin2(1'b1), .pin3(instruction[5]), .pin4(_74157_1_pin4), .pin5(1'b0),
    .pin6(1'b0), .pin8(1'b0), .pin10(1'b0), .pin11(1'b0), .pin13(1'b0), .pin14(1'b0), .pin15(1'b0),
    .pin16(1'b1));  // open: pin7, pin9, pin12
  Mux16 mux16_1 (.sel(instruction[15]), .in0(instruction), .in1(outM), .out(mux16_1_out));
  _7408 _7408_1 (
    .pin1(instruction[4]), .pin2(instruction[15]), .pin3(_7408_1_pin3), .pin4(instruction[15]),
    .pin5(instruction[3]), .pin6(writeM), .pin7(1'b0), .pin9(1'b1), .pin10(1'b1), .pin12(1'b1), .pin13(1'b1),
    .pin14(1'b1));  // open: pin8, pin11
  reg_16 regA (
    .data_in(mux16_1_out), .clk_in(clk), .load(_74157_1_pin4), .reset(1'b0),
    .data_out({regAvalue[15], AddressM}));
  Mux16 mux16_2 (.sel(instruction[12]), .in0({regAvalue[15], AddressM}), .in1(in_m), .out(mux16_2_out));
  reg_16 regD (.data_in(outM), .clk_in(clk), .load(_7408_1_pin3), .reset(1'b0), .data_out(regDvalue));
  ALU alu_1 (
    .x(regDvalue), .y(mux16_2_out), .f(instruction[7]), .nx(instruction[10]), .ny(instruction[8]),
    .zx(instruction[11]), .zy(instruction[9]), .no(instruction[6]), .out(outM), .ng(alu_1_ng), .zr(alu_1_zr));
  _7408 _7408_2 (
    .pin1(instruction[0]), .pin2(instruction[15]), .pin3(_7408_2_pin3), .pin4(instruction[1]),
    .pin5(instruction[15]), .pin6(_7408_2_pin6), .pin7(1'b0), .pin8(_7408_2_pin8), .pin9(instruction[2]),
    .pin10(instruction[15]), .pin12(1'b1), .pin13(1'b1), .pin14(1'b1));  // open: pin11
  _7408 _7408_3 (
    .pin1(_7408_2_pin6), .pin2(alu_1_zr), .pin3(_7408_3_pin3), .pin4(_7408_2_pin8), .pin5(alu_1_ng),
    .pin6(_7408_3_pin6), .pin7(1'b0), .pin8(_7408_3_pin8), .pin9(_7408_3_pin9), .pin10(_7408_2_pin3),
    .pin12(1'b1), .pin13(1'b1), .pin14(1'b1));  // open: pin11
  _7432 _7432_1 (
    .pin1(alu_1_zr), .pin2(alu_1_ng), .pin3(_7432_1_pin3), .pin4(_7408_3_pin3), .pin5(_7408_3_pin6),
    .pin6(_7432_1_pin6), .pin7(1'b0), .pin8(_7432_1_pin8), .pin9(_7408_3_pin8), .pin10(_7432_1_pin6),
    .pin12(1'b1), .pin13(1'b1), .pin14(1'b1));  // open: pin11
  _7404 _7404_1 (
    .pin1(_7432_1_pin3), .pin2(_7408_3_pin9), .pin3(1'b0), .pin5(1'b0), .pin7(1'b0), .pin9(1'b1),
    .pin11(1'b1), .pin13(1'b1), .pin14(1'b1));  // open: pin4, pin6, pin8, pin10, pin12
  PC pc_1 (
    .reset(reset), .data_in({regAvalue[15], AddressM}), .load(_7432_1_pin8), .inc(1'b1), .clk_in(clk),
    .count_out({pc_1_count_out[15], pc}));

  assign regAvalue[14:0] = AddressM;
endmodule
