// Digital circuit Computer.dig as structural Verilog
module Computer (
  input  clk,
  input  pc_reset,
  input  [15:0] Keyboard,
  output [15:0] RegA_value,
  output [15:0] RegD_value,
  output [15:0] PC_value
);

  wire [14:0] undriven;

  Memory memory_1 ();  // open: Address
  CPU cpu_1 ();  // open: instruction, in_m, clk, reset, outM, writeM, AddressM, pc, regAvalue, regDvalue
  ROM rom_1 (.Address_in(undriven));  // open: instruction_out

  // Notes on the sheet:
  //   clk: Hz: 5
  //   contents of *lower (hex, n*v repeats v):
  //   /Users/surya/Documents/GitHub/nand2tetris/Physical Design/Mult (1)_lower.hex false
  //   contents of *higher (hex, n*v repeats v):
  //   /Users/surya/Documents/GitHub/nand2tetris/Physical Design/Mult (1)_upper.hex false
endmodule
