// Digital circuit Memory.dig as structural Verilog
module Memory (
  input  [15:0] Keyboard,
  input  [14:0] Address,
  input  [15:0] data_in,
  input  clk,
  input  load,
  output [15:0] data_out
);

  wire _7404_1_pin2, _7404_1_pin12, _7408_1_pin3, _7408_1_pin8, _7408_1_pin10;
  wire [15:0] mux16_1_out;
  wire [31:0] RAM0_p7, RAM1_p7;

  _7404 _7404_1 (
    .pin1(Address[13]), .pin2(_7404_1_pin2), .pin3(1'b0), .pin5(1'b0), .pin7(1'b0), .pin9(1'b0),
    .pin11(1'b0), .pin12(_7404_1_pin12), .pin13(Address[14]), .pin14(1'b1));  // open: pin4, pin6, pin8, pin10
  _7408 _7408_1 (
    .pin1(_7404_1_pin12), .pin2(load), .pin3(_7408_1_pin3), .pin4(1'b0), .pin5(1'b0), .pin7(1'b0),
    .pin8(_7408_1_pin8), .pin9(_7404_1_pin2), .pin10(_7408_1_pin10), .pin11(_7408_1_pin10),
    .pin12(Address[14]), .pin13(load), .pin14(1'b1));  // open: pin6
  // RAM32Bit #(.generic("addrBits := 14; dataBits := 16;")) RAM0: pin names not known; wires that end beside it: Address[13:0], {{16{1'b0}}, data_in}, _7408_1_pin3, 2'b00, 1'b0, clk, RAM0_p7
  // RAM32Bit #(.generic("addrBits := 13; dataBits := 16;")) RAM1: pin names not known; wires that end beside it: Address[12:0], {{16{1'b0}}, data_in}, _7408_1_pin8, 2'b00, 1'b0, clk, RAM1_p7
  Mux16 mux16_1 (.sel(Address[13]), .in0(RAM1_p7[15:0]), .in1(Keyboard), .out(mux16_1_out));
  Mux16 mux16_2 (.sel(Address[14]), .in0(RAM0_p7[15:0]), .in1(mux16_1_out), .out(data_out));
endmodule
