// Digital circuit Mux16.dig as structural Verilog
module Mux16 (
  input  sel,
  input  [15:0] in0,
  input  [15:0] in1,
  output [15:0] out
);

  _74157 _74157_1 (
    .pin1(sel), .pin2(in0[0]), .pin3(in1[0]), .pin4(out[0]), .pin5(in0[1]), .pin6(in1[1]), .pin7(out[1]),
    .pin8(1'b0), .pin9(out[2]), .pin10(in1[2]), .pin11(in0[2]), .pin12(out[3]), .pin13(in1[3]),
    .pin14(in0[3]), .pin15(1'b0), .pin16(1'b1));
  _74157 _74157_2 (
    .pin1(sel), .pin2(in0[4]), .pin3(in1[4]), .pin4(out[4]), .pin5(in0[5]), .pin6(in1[5]), .pin7(out[5]),
    .pin8(1'b0), .pin9(out[6]), .pin10(in1[6]), .pin11(in0[6]), .pin12(out[7]), .pin13(in1[7]),
    .pin14(in0[7]), .pin15(1'b0), .pin16(1'b1));
  _74157 _74157_3 (
    .pin1(sel), .pin2(in0[8]), .pin3(in1[8]), .pin4(out[8]), .pin5(in0[9]), .pin6(in1[9]), .pin7(out[9]),
    .pin8(1'b0), .pin9(out[10]), .pin10(in1[10]), .pin11(in0[10]), .pin12(out[11]), .pin13(in1[11]),
    .pin14(in0[11]), .pin15(1'b0), .pin16(1'b1));
  _74157 _74157_4 (
    .pin1(sel), .pin2(in0[12]), .pin3(in1[12]), .pin4(out[12]), .pin5(in0[13]), .pin6(in1[13]),
    .pin7(out[13]), .pin8(1'b0), .pin9(out[14]), .pin10(in1[14]), .pin11(in0[14]), .pin12(out[15]),
    .pin13(in1[15]), .pin14(in0[15]), .pin15(1'b0), .pin16(1'b1));
endmodule
