// Digital circuit PC.dig as structural Verilog
module PC (
  input  reset,
  input  [15:0] data_in,
  input  load,
  input  inc,
  input  clk_in,
  output [15:0] count_out
);

  wire _7432_1_pin3, _7432_1_pin6;
  wire [15:0] add1_1_x_plus_1, mux16_1_out, mux16_2_out, mux16_3_out;

  Mux16 mux16_1 (.sel(inc), .in0(count_out), .in1(add1_1_x_plus_1), .out(mux16_1_out));
  Mux16 mux16_2 (.sel(load), .in0(mux16_1_out), .in1(data_in), .out(mux16_2_out));
  _7432 _7432_1 (
    .pin1(inc), .pin2(load), .pin3(_7432_1_pin3), .pin4(_7432_1_pin3), .pin5(reset), .pin6(_7432_1_pin6),
    .pin7(1'b0), .pin9(1'b1), .pin10(1'b1), .pin12(1'b1), .pin13(1'b1), .pin14(1'b1));  // open: pin8, pin11
  Mux16 mux16_3 (.sel(reset), .in0(mux16_2_out), .in1({16{1'b0}}), .out(mux16_3_out));
  reg_16 reg_16_1 (.data_in(mux16_3_out), .clk_in(clk_in), .load(_7432_1_pin6), .reset(1'b0), .data_out(count_out));
  Add1 add1_1 (.x(count_out), .x_plus_1(add1_1_x_plus_1));
endmodule
