// Digital circuit ROM.dig as structural Verilog
module ROM (
  input  [14:0] Address_in,
  output [15:0] instruction_out
);

  // _28c256 lower: pin names not known; wires that end beside it: Address_in[14], Address_in[12], Address_in[7], Address_in[6], Address_in[5], Address_in[4], Address_in[3], Address_in[2], Address_in[1], Address_in[0], instruction_out[0], instruction_out[1], instruction_out[2], 1'b1, 1'b1, Address_in[13], Address_in[8], Address_in[9], Address_in[11], 1'b0, Address_in[10], 1'b0, instruction_out[7]
  // _28c256 higher: pin names not known; wires that end beside it: 1'b0, Address_in[14], Address_in[12], Address_in[7], Address_in[6], Address_in[5], Address_in[4], Address_in[3], Address_in[2], Address_in[1], Address_in[0], instruction_out[8], instruction_out[9], instruction_out[10], 1'b0, 1'b1, 1'b1, Address_in[13], Address_in[8], Address_in[9], Address_in[11], 1'b0, Address_in[10], 1'b0, instruction_out[15]

  // Notes on the sheet:
  //   contents of *lower (hex, n*v repeats v):
  //   /Users/surya/Documents/GitHub/nand2tetris/Physical Design/lower.hex false
  //   contents of *higher (hex, n*v repeats v):
  //   /Users/surya/Documents/GitHub/nand2tetris/Physical Design/upper.hex false
endmodule
