// Digital circuit reg_16.dig as structural Verilog
module reg_16 (
  input  [15:0] data_in,
  input  clk_in,
  input  load,
  input  reset,
  output [15:0] data_out
);

  wire _7404_1_pin2;
  wire [7:0] mux16_1_out, mux16_1_out_2;

  Mux16 mux16_1 (.sel(load), .in0(data_out), .in1(data_in), .out({mux16_1_out_2, mux16_1_out}));
  _7404 _7404_1 (
    .pin1(reset), .pin2(_7404_1_pin2), .pin3(1'b0), .pin5(1'b0), .pin7(1'b0), .pin9(1'b1), .pin11(1'b1),
    .pin13(1'b1), .pin14(1'b1));  // open: pin4, pin6, pin8, pin10, pin12
  _74273 _74273_1 (
    .pin1(_7404_1_pin2), .pin2(data_out[0]), .pin3(mux16_1_out[0]), .pin4(mux16_1_out[1]),
    .pin5(data_out[1]), .pin6(data_out[2]), .pin7(mux16_1_out[2]), .pin8(mux16_1_out[3]), .pin9(data_out[3]),
    .pin10(1'b0), .pin11(clk_in), .pin12(data_out[4]), .pin13(mux16_1_out[4]), .pin14(mux16_1_out[5]),
    .pin15(data_out[5]), .pin16(data_out[6]), .pin17(mux16_1_out[6]), .pin18(mux16_1_out[7]),
    .pin19(data_out[7]), .pin20(1'b1));
  _74273 _74273_2 (
    .pin1(_7404_1_pin2), .pin2(data_out[8]), .pin3(mux16_1_out_2[0]), .pin4(mux16_1_out_2[1]),
    .pin5(data_out[9]), .pin6(data_out[10]), .pin7(mux16_1_out_2[2]), .pin8(mux16_1_out_2[3]),
    .pin9(data_out[11]), .pin10(1'b0), .pin11(clk_in), .pin12(data_out[12]), .pin13(mux16_1_out_2[4]),
    .pin14(mux16_1_out_2[5]), .pin15(data_out[13]), .pin16(data_out[14]), .pin17(mux16_1_out_2[6]),
    .pin18(mux16_1_out_2[7]), .pin19(data_out[15]), .pin20(1'b1));
endmodule
