// Digital circuit x_inv.dig as structural Verilog
module x_inv (
  input  [15:0] x_in,
  output [15:0] x_out
);

  wire _7404_3_pin11, _7404_3_pin13;

  _7404 _7404_1 (
    .pin1(x_in[0]), .pin2(x_out[0]), .pin3(x_in[1]), .pin4(x_out[1]), .pin5(x_in[2]), .pin6(x_out[2]),
    .pin7(1'b0), .pin8(x_out[3]), .pin9(x_in[3]), .pin10(x_out[4]), .pin11(x_in[4]), .pin12(x_out[5]),
    .pin13(x_in[5]), .pin14(1'b1));
  _7404 _7404_2 (
    .pin1(x_in[6]), .pin2(x_out[6]), .pin3(x_in[7]), .pin4(x_out[7]), .pin5(x_in[8]), .pin6(x_out[8]),
    .pin7(1'b0), .pin8(x_out[11]), .pin9(x_in[9]), .pin10(x_out[10]), .pin11(x_in[10]), .pin12(x_out[9]),
    .pin13(x_in[11]), .pin14(1'b1));
  _7404 _7404_3 (
    .pin1(x_in[15]), .pin2(x_out[15]), .pin3(x_in[14]), .pin4(x_out[14]), .pin5(x_in[13]), .pin6(x_out[13]),
    .pin7(1'b0), .pin8(x_out[12]), .pin9(x_in[12]), .pin11(_7404_3_pin11), .pin13(_7404_3_pin13), .pin14(1'b1));  // open: pin10, pin12
  // NotConnected on _7404_3_pin13
  // NotConnected on _7404_3_pin11
endmodule
