// Digital circuit xproc.dig as structural Verilog
module xproc (
  input  [15:0] X,
  input  zx,
  input  nx,
  output [15:0] xproc
);

  wire [15:0] mux16_1_out, x_inv_1_x_out;

  Mux16 mux16_1 (.sel(zx), .in0(X), .in1({16{1'b0}}), .out(mux16_1_out));
  x_inv x_inv_1 (.x_in(mux16_1_out), .x_out(x_inv_1_x_out));
  Mux16 mux16_2 (.sel(nx), .in0(mux16_1_out), .in1(x_inv_1_x_out), .out(xproc));
endmodule
